# Fritzing sketch reed_activated_relay (saved by Fritzing 0.9.2b)
breadboards: 1

parts:
  K1 = Relay [part_number=FRS1B-S package=THT]
  LED1 = LED - 5mm [color="Red (633nm)" package="5 mm [THT]"]
  V1 = AC Power [voltage=5 frequency=60]
  U1 = attiny85 [package=dip]
  S1 = SWITCH-MOMENTARY-2 [package=reed_switch_pth]
  R1 = Resistor [tolerance=±5% resistance=10k package="0402 [SMD]"]

nets:
  N1: K1.A, LED1.cathode
  N2: K1.COIL1, U1.Pin_4, S1.2
  N3: K1.C1, V1.V+
  N4: K1.COIL2, U1.Pin_5
  N5: LED1.anode, V1.V-
  N6: U1.Pin_2, S1.1, R1.Pin_0
  N7: U1.Pin_8, R1.Pin_1
